// Logisim project cpu.circ as structural Verilog
module _10_bit_Register_File (
  input  [9:0] Write_Data,
  input  [1:0] RS,
  input  [1:0] RD,
  input  WE,
  input  in_5,
  input  [1:0] RT,
  output [9:0] Data_1,
  output [9:0] Data_2
);

  wire and_1_out, and_2_out, and_3_out, and_4_out, decoder_1_out0, decoder_1_out1, decoder_1_out2,
       decoder_1_out3;
  wire [9:0] register_1_q, register_2_q, register_3_q, register_4_q;

  Decoder #(.select(2), .enable("false")) decoder_1 (
    .out0(decoder_1_out0), .out1(decoder_1_out1), .out2(decoder_1_out2), .out3(decoder_1_out3), .sel(RD));
  and and_1 (and_1_out, decoder_1_out0, WE);
  and and_2 (and_2_out, decoder_1_out1, WE);
  and and_3 (and_3_out, decoder_1_out2, WE);
  and and_4 (and_4_out, decoder_1_out3, WE);
  Register #(.width(10)) register_1 (.D(Write_Data), .en(and_1_out), .Q(register_1_q), .clk(in_5));  // open: clr
  Register #(.width(10)) register_2 (.D(Write_Data), .en(and_2_out), .Q(register_2_q), .clk(in_5));  // open: clr
  Register #(.width(10)) register_3 (.D(Write_Data), .en(and_3_out), .Q(register_3_q), .clk(in_5));  // open: clr
  Register #(.width(10)) register_4 (.D(Write_Data), .en(and_4_out), .Q(register_4_q), .clk(in_5));  // open: clr
  Multiplexer #(.select(2), .width(10), .enable("false")) multiplexer_1 (
    .in0(register_1_q), .in1(register_2_q), .in2(register_3_q), .in3(register_4_q), .out(Data_1), .sel(RS));
  Multiplexer #(.select(2), .width(10), .enable("false")) multiplexer_2 (
    .in0(register_1_q), .in1(register_2_q), .in2(register_3_q), .in3(register_4_q), .out(Data_2), .sel(RT));
endmodule
